// Digital circuit ALU-8bit.dig as structural Verilog
module ALU_8bit (
  input  Soma,
  input  Sub,
  input  Multi,
  input  Div,
  input  NAND,
  input  XOR,
  input  Right,
  input  Left,
  input  [7:0] A,
  input  [7:0] B,
  input  Load,
  output [7:0] S
);

  wire anda0, anda1, anda2, anda3, anda4, anda5, anda6, anda7, andb0, andb1, andb2, andb3, andb4, andb5,
       andb6, andb7, co_soma, diva0, diva1, diva2, diva3, diva4, diva5, diva6, diva7, divb0, divb1, divb2,
       divb3, divb4, divb5, divb6, divb7, multia0, multia1, multia2, multia3, multia4, multia5, multia6,
       multia7, multib0, multib1, multib2, multib3, multib4, multib5, multib6, multib7,
       multiplicador_8bits_1_s8, multiplicador_8bits_1_s9, multiplicador_8bits_1_s10,
       multiplicador_8bits_1_s11, multiplicador_8bits_1_s12, multiplicador_8bits_1_s13,
       multiplicador_8bits_1_s14, multiplicador_8bits_1_s15, nand_8bits_1_s0, nand_8bits_1_s1,
       nand_8bits_1_s2, nand_8bits_1_s3, nand_8bits_1_s4, nand_8bits_1_s5, nand_8bits_1_s6, nand_8bits_1_s7,
       shift_left_1_s0, shift_left_1_s1, shift_left_1_s2, shift_left_1_s3, shift_left_1_s4, shift_left_1_s5,
       shift_left_1_s6, shift_left_1_s7, shift_right_1_s0, shift_right_1_s1, shift_right_1_s2,
       shift_right_1_s3, shift_right_1_s4, shift_right_1_s5, shift_right_1_s6, shift_right_1_s7,
       soma_sub_8bits_1_s0, soma_sub_8bits_1_s1, soma_sub_8bits_1_s2, soma_sub_8bits_1_s3,
       soma_sub_8bits_1_s4, soma_sub_8bits_1_s5, soma_sub_8bits_1_s6, soma_sub_8bits_1_s7, somaA0, somaA1,
       somaA2, somaA3, somaA4, somaA5, somaA6, somaA7, somaB0, somaB1, somaB2, somaB3, somaB4, somaB5,
       somaB6, somaB7, xora0, xora1, xora2, xora3, xora4, xora5, xora6, xora7, xorb0, xorb1, xorb2, xorb3,
       xorb4, xorb5, xorb6, xorb7, xs0, xs1, xs2, xs3, xs4, xs5, xs6, xs7;
  wire [7:0] load_t, r_div, s_div, s_multi, s_nand, s_sl, s_soma, s_sr, s_sub, s_xor;

  and and_1 (load_t[0], Load, A[0]);
  and and_2 (load_t[1], Load, A[1]);
  and and_3 (load_t[2], Load, A[2]);
  and and_4 (load_t[3], Load, A[3]);
  and and_5 (load_t[4], Load, A[4]);
  and and_6 (load_t[5], Load, A[5]);
  and and_7 (load_t[6], Load, A[6]);
  and and_8 (load_t[7], Load, A[7]);
  and and_9 (somaA7, Soma, A[7]);
  and and_10 (somaB7, Soma, B[7]);
  and and_11 (somaA6, Soma, A[6]);
  and and_12 (somaB6, Soma, B[6]);
  and and_13 (somaA5, Soma, A[5]);
  and and_14 (somaB5, Soma, B[5]);
  and and_15 (somaA4, Soma, A[4]);
  and and_16 (somaB4, Soma, B[4]);
  and and_17 (somaA3, Soma, A[3]);
  and and_18 (somaB3, Soma, B[3]);
  and and_19 (somaA2, Soma, A[2]);
  and and_20 (somaB2, Soma, B[2]);
  and and_21 (somaA1, Soma, A[1]);
  and and_22 (somaB1, Soma, B[1]);
  and and_23 (somaA0, Soma, A[0]);
  and and_24 (somaB0, Soma, B[0]);
  soma_8bits soma_8bits_1 (
    .A7(somaA7), .B7(somaB7), .A6(somaA6), .B6(somaB6), .A5(somaA5), .B5(somaB5), .A4(somaA4), .B4(somaB4),
    .A3(somaA3), .B3(somaB3), .A2(somaA2), .B2(somaB2), .A1(somaA1), .B1(somaB1), .A0(somaA0), .B0(somaB0),
    .S0(s_soma[0]), .S1(s_soma[1]), .S2(s_soma[2]), .S3(s_soma[3]), .S4(s_soma[4]), .S5(s_soma[5]),
    .S6(s_soma[6]), .S7(s_soma[7]), .Co(co_soma));
  soma_sub_8bits soma_sub_8bits_1 (
    .SUB(Sub), .B0(B[0]), .B1(B[1]), .B2(B[2]), .B3(B[3]), .B4(B[4]), .B5(B[5]), .B6(B[6]), .B7(B[7]),
    .A0(A[0]), .A1(A[1]), .A2(A[2]), .A3(A[3]), .A4(A[4]), .A5(A[5]), .A6(A[6]), .A7(A[7]),
    .S0(soma_sub_8bits_1_s0), .S1(soma_sub_8bits_1_s1), .S2(soma_sub_8bits_1_s2), .S3(soma_sub_8bits_1_s3),
    .S4(soma_sub_8bits_1_s4), .S5(soma_sub_8bits_1_s5), .S6(soma_sub_8bits_1_s6), .S7(soma_sub_8bits_1_s7));
  and and_25 (s_sub[0], Sub, soma_sub_8bits_1_s0);
  and and_26 (s_sub[1], Sub, soma_sub_8bits_1_s1);
  and and_27 (s_sub[2], Sub, soma_sub_8bits_1_s2);
  and and_28 (s_sub[3], Sub, soma_sub_8bits_1_s3);
  and and_29 (s_sub[4], Sub, soma_sub_8bits_1_s4);
  and and_30 (s_sub[5], Sub, soma_sub_8bits_1_s5);
  and and_31 (s_sub[6], Sub, soma_sub_8bits_1_s6);
  and and_32 (s_sub[7], Sub, soma_sub_8bits_1_s7);
  and and_33 (multia0, Multi, A[0]);
  and and_34 (multia1, Multi, A[1]);
  and and_35 (multia2, Multi, A[2]);
  and and_36 (multia3, Multi, A[3]);
  and and_37 (multia4, Multi, A[4]);
  and and_38 (multia5, Multi, A[5]);
  and and_39 (multia6, Multi, A[6]);
  and and_40 (multia7, Multi, A[7]);
  and and_41 (multib0, Multi, B[0]);
  and and_42 (multib1, Multi, B[1]);
  and and_43 (multib2, Multi, B[2]);
  and and_44 (multib3, Multi, B[3]);
  and and_45 (multib4, Multi, B[4]);
  and and_46 (multib5, Multi, B[5]);
  and and_47 (multib6, Multi, B[6]);
  and and_48 (multib7, Multi, B[7]);
  multiplicador_8bits multiplicador_8bits_1 (
    .A0(multia0), .A1(multia1), .A2(multia2), .A3(multia3), .A4(multia4), .A5(multia5), .A6(multia6),
    .A7(multia7), .B0(multib0), .B1(multib1), .B2(multib2), .B3(multib3), .B4(multib4), .B5(multib5),
    .B6(multib6), .B7(multib7), .S0(s_multi[0]), .S1(s_multi[1]), .S2(s_multi[2]), .S3(s_multi[3]),
    .S4(s_multi[4]), .S5(s_multi[5]), .S6(s_multi[6]), .S7(s_multi[7]), .S8(multiplicador_8bits_1_s8),
    .S9(multiplicador_8bits_1_s9), .S10(multiplicador_8bits_1_s10), .S11(multiplicador_8bits_1_s11),
    .S12(multiplicador_8bits_1_s12), .S13(multiplicador_8bits_1_s13), .S14(multiplicador_8bits_1_s14),
    .S15(multiplicador_8bits_1_s15));
  and and_49 (diva0, Div, A[0]);
  and and_50 (diva1, Div, A[1]);
  and and_51 (diva2, Div, A[2]);
  and and_52 (diva3, Div, A[3]);
  and and_53 (diva4, Div, A[4]);
  and and_54 (diva5, Div, A[5]);
  and and_55 (diva6, Div, A[6]);
  and and_56 (diva7, Div, A[7]);
  and and_57 (divb0, Div, B[0]);
  and and_58 (divb1, Div, B[1]);
  and and_59 (divb2, Div, B[2]);
  and and_60 (divb3, Div, B[3]);
  and and_61 (divb4, Div, B[4]);
  and and_62 (divb5, Div, B[5]);
  and and_63 (divb6, Div, B[6]);
  and and_64 (divb7, Div, B[7]);
  Div #(.Bits(8)) div_1 (
    .a({diva7, diva6, diva5, diva4, diva3, diva2, diva1, diva0}),
    .b({divb7, divb6, divb5, divb4, divb3, divb2, divb1, divb0}), .q(s_div), .r(r_div));
  and and_65 (anda0, NAND, A[0]);
  and and_66 (anda1, NAND, A[1]);
  and and_67 (anda2, NAND, A[2]);
  and and_68 (anda3, NAND, A[3]);
  and and_69 (anda4, NAND, A[4]);
  and and_70 (anda5, NAND, A[5]);
  and and_71 (anda6, NAND, A[6]);
  and and_72 (anda7, NAND, A[7]);
  and and_73 (andb0, NAND, B[0]);
  and and_74 (andb1, NAND, B[1]);
  and and_75 (andb2, NAND, B[2]);
  and and_76 (andb3, NAND, B[3]);
  and and_77 (andb4, NAND, B[4]);
  and and_78 (andb5, NAND, B[5]);
  and and_79 (andb6, NAND, B[6]);
  and and_80 (andb7, NAND, B[7]);
  NAND_8bits nand_8bits_1 (
    .A0(anda0), .A1(anda1), .A2(anda2), .A3(anda3), .A4(anda4), .A5(anda5), .A6(anda6), .A7(anda7),
    .B0(andb0), .B1(andb1), .B2(andb2), .B3(andb3), .B4(andb4), .B5(andb5), .B6(andb6), .B7(andb7),
    .S0(nand_8bits_1_s0), .S1(nand_8bits_1_s1), .S2(nand_8bits_1_s2), .S3(nand_8bits_1_s3),
    .S4(nand_8bits_1_s4), .S5(nand_8bits_1_s5), .S6(nand_8bits_1_s6), .S7(nand_8bits_1_s7));
  and and_81 (s_nand[0], NAND, nand_8bits_1_s0);
  and and_82 (s_nand[1], NAND, nand_8bits_1_s1);
  and and_83 (s_nand[2], NAND, nand_8bits_1_s2);
  and and_84 (s_nand[3], NAND, nand_8bits_1_s3);
  and and_85 (s_nand[4], NAND, nand_8bits_1_s4);
  and and_86 (s_nand[5], NAND, nand_8bits_1_s5);
  and and_87 (s_nand[6], NAND, nand_8bits_1_s6);
  and and_88 (s_nand[7], NAND, nand_8bits_1_s7);
  and and_89 (xora0, XOR, A[0]);
  and and_90 (xora1, XOR, A[1]);
  and and_91 (xora2, XOR, A[2]);
  and and_92 (xora3, XOR, A[3]);
  and and_93 (xora4, XOR, A[4]);
  and and_94 (xora5, XOR, A[5]);
  and and_95 (xora6, XOR, A[6]);
  and and_96 (xora7, XOR, A[7]);
  and and_97 (xorb0, XOR, B[0]);
  and and_98 (xorb1, XOR, B[1]);
  and and_99 (xorb2, XOR, B[2]);
  and and_100 (xorb3, XOR, B[3]);
  and and_101 (xorb4, XOR, B[4]);
  and and_102 (xorb5, XOR, B[5]);
  and and_103 (xorb6, XOR, B[6]);
  and and_104 (xorb7, XOR, B[7]);
  XOR_8bits xor_8bits_1 (
    .A0(xora0), .A1(xora1), .A2(xora2), .A3(xora3), .A4(xora4), .A5(xora5), .A6(xora6), .A7(xora7),
    .B0(xorb0), .B1(xorb1), .B2(xorb2), .B3(xorb3), .B4(xorb4), .B5(xorb5), .B6(xorb6), .B7(xorb7),
    .S0(s_xor[0]), .S1(s_xor[1]), .S2(s_xor[2]), .S3(s_xor[3]), .S4(s_xor[4]), .S5(s_xor[5]), .S6(s_xor[6]),
    .S7(s_xor[7]));
  XOR_8bits xor_8bits_2 (
    .A0(A[0]), .A1(A[1]), .A2(A[2]), .A3(A[3]), .A4(A[4]), .A5(A[5]), .A6(A[6]), .A7(A[7]), .B0(B[0]),
    .B1(B[1]), .B2(B[2]), .B3(B[3]), .B4(B[4]), .B5(B[5]), .B6(B[6]), .B7(B[7]), .S0(xs0), .S1(xs1),
    .S2(xs2), .S3(xs3), .S4(xs4), .S5(xs5), .S6(xs6), .S7(xs7));
  shift_left shift_left_1 (
    .A0(xs0), .A1(xs1), .A2(xs2), .A3(xs3), .A4(xs4), .A5(xs5), .A6(xs6), .A7(xs7), .S0(shift_left_1_s0),
    .S1(shift_left_1_s1), .S2(shift_left_1_s2), .S3(shift_left_1_s3), .S4(shift_left_1_s4),
    .S5(shift_left_1_s5), .S6(shift_left_1_s6), .S7(shift_left_1_s7));
  and and_105 (s_sl[0], Left, shift_left_1_s0);
  and and_106 (s_sl[1], Left, shift_left_1_s1);
  and and_107 (s_sl[2], Left, shift_left_1_s2);
  and and_108 (s_sl[3], Left, shift_left_1_s3);
  and and_109 (s_sl[4], Left, shift_left_1_s4);
  and and_110 (s_sl[5], Left, shift_left_1_s5);
  and and_111 (s_sl[6], Left, shift_left_1_s6);
  and and_112 (s_sl[7], Left, shift_left_1_s7);
  shift_right shift_right_1 (
    .A0(xs0), .A1(xs1), .A2(xs2), .A3(xs3), .A4(xs4), .A5(xs5), .A6(xs6), .A7(xs7), .S0(shift_right_1_s0),
    .S1(shift_right_1_s1), .S2(shift_right_1_s2), .S3(shift_right_1_s3), .S4(shift_right_1_s4),
    .S5(shift_right_1_s5), .S6(shift_right_1_s6), .S7(shift_right_1_s7));
  and and_113 (s_sr[0], Right, shift_right_1_s0);
  and and_114 (s_sr[1], Right, shift_right_1_s1);
  and and_115 (s_sr[2], Right, shift_right_1_s2);
  and and_116 (s_sr[3], Right, shift_right_1_s3);
  and and_117 (s_sr[4], Right, shift_right_1_s4);
  and and_118 (s_sr[5], Right, shift_right_1_s5);
  and and_119 (s_sr[6], Right, shift_right_1_s6);
  and and_120 (s_sr[7], Right, shift_right_1_s7);
  assign S = s_soma ^ s_sub ^ s_multi ^ s_div ^ load_t ^ s_nand ^ s_xor ^ s_sr ^ s_sl;  // XOr xor_1, 8 bits wide
endmodule
