// Digital circuit ALU-visual.dig as structural Verilog
module ALU_visual (
  input  [7:0] N,
  input  En,
  input  Clk,
  input  [2:0] Op,
  output [7:0] Ac,
  output [7:0] Mq
);

  wire [7:0] mult_ac, mult_mq, multiplexer_1_out, multiplexer_2_out, \nand , quo, resto, sl, soma, sr, sub,
       \xor ;

  soma_8bits soma_8bits_1 (
    .A7(Ac[7]), .B7(N[7]), .A6(Ac[6]), .B6(N[6]), .A5(Ac[5]), .B5(N[5]), .A4(Ac[4]), .B4(N[4]), .A3(Ac[3]),
    .B3(N[3]), .A2(Ac[2]), .B2(N[2]), .A1(Ac[1]), .B1(N[1]), .A0(Ac[0]), .B0(N[0]), .S0(soma[0]),
    .S1(soma[1]), .S2(soma[2]), .S3(soma[3]), .S4(soma[4]), .S5(soma[5]), .S6(soma[6]), .S7(soma[7]));  // open: Co
  Multiplexer #(.Selector_Bits(3), .Bits(8)) multiplexer_1 (
    .sel(Op), .in_0(soma), .in_1(sub), .in_2(mult_ac), .in_3(resto), .in_4(\nand ), .in_5(\xor ), .in_6(sl),
    .in_7(sr), .out(multiplexer_1_out));
  Register #(.Bits(8)) register_1 (.D(multiplexer_1_out), .C(Clk), .en(En), .Q(Ac));
  soma_sub_8bits soma_sub_8bits_1 (
    .SUB(1'b1), .B0(N[0]), .B1(N[1]), .B2(N[2]), .B3(N[3]), .B4(N[4]), .B5(N[5]), .B6(N[6]), .B7(N[7]),
    .A0(Ac[0]), .A1(Ac[1]), .A2(Ac[2]), .A3(Ac[3]), .A4(Ac[4]), .A5(Ac[5]), .A6(Ac[6]), .A7(Ac[7]),
    .S0(sub[0]), .S1(sub[1]), .S2(sub[2]), .S3(sub[3]), .S4(sub[4]), .S5(sub[5]), .S6(sub[6]), .S7(sub[7]));
  Multiplexer #(.Selector_Bits(3), .Bits(8)) multiplexer_2 (
    .sel(Op), .in_0(Mq), .in_1(Mq), .in_2(mult_mq), .in_3(quo), .in_4(Mq), .in_5(Mq), .in_6(Mq), .in_7(Mq),
    .out(multiplexer_2_out));
  Register #(.Bits(8)) register_2 (.D(multiplexer_2_out), .C(Clk), .en(En), .Q(Mq));
  Mul #(.Bits(8)) mul_1 (.a(Ac), .b(N), .mul({mult_mq, mult_ac}));
  Div #(.Bits(8)) div_1 (.a(Ac), .b(N), .q(quo), .r(resto));
  shift_left shift_left_1 (
    .A0(Ac[0]), .A1(Ac[1]), .A2(Ac[2]), .A3(Ac[3]), .A4(Ac[4]), .A5(Ac[5]), .A6(Ac[6]), .A7(Ac[7]),
    .S0(sl[0]), .S1(sl[1]), .S2(sl[2]), .S3(sl[3]), .S4(sl[4]), .S5(sl[5]), .S6(sl[6]), .S7(sl[7]));
  shift_right shift_right_1 (
    .A0(Ac[0]), .A1(Ac[1]), .A2(Ac[2]), .A3(Ac[3]), .A4(Ac[4]), .A5(Ac[5]), .A6(Ac[6]), .A7(Ac[7]),
    .S0(sr[0]), .S1(sr[1]), .S2(sr[2]), .S3(sr[3]), .S4(sr[4]), .S5(sr[5]), .S6(sr[6]), .S7(sr[7]));
  NAND_8bits nand_8bits_1 (
    .A0(Ac[0]), .A1(Ac[1]), .A2(Ac[2]), .A3(Ac[3]), .A4(Ac[4]), .A5(Ac[5]), .A6(Ac[6]), .A7(Ac[7]),
    .B0(N[0]), .B1(N[1]), .B2(N[2]), .B3(N[3]), .B4(N[4]), .B5(N[5]), .B6(N[6]), .B7(N[7]), .S0(\nand [0]),
    .S1(\nand [1]), .S2(\nand [2]), .S3(\nand [3]), .S4(\nand [4]), .S5(\nand [5]), .S6(\nand [6]),
    .S7(\nand [7]));
  XOR_8bits xor_8bits_1 (
    .A0(Ac[0]), .A1(Ac[1]), .A2(Ac[2]), .A3(Ac[3]), .A4(Ac[4]), .A5(Ac[5]), .A6(Ac[6]), .A7(Ac[7]),
    .B0(N[0]), .B1(N[1]), .B2(N[2]), .B3(N[3]), .B4(N[4]), .B5(N[5]), .B6(N[6]), .B7(N[7]), .S0(\xor [0]),
    .S1(\xor [1]), .S2(\xor [2]), .S3(\xor [3]), .S4(\xor [4]), .S5(\xor [5]), .S6(\xor [6]), .S7(\xor [7]));
endmodule
