// Digital circuit CPU-8BITS.dig as structural Verilog
module CPU_8BITS (
  input  [3:0] PC,
  output [7:0] S
);

  wire button_1_out;
  wire [7:0] alu_visual_1_r;
  wire [11:0] eepromdualport_1_d;

  Button button_1 (.out(button_1_out));
  EEPROMDualPort #(.AddrBits(4), .Bits(12)) eepromdualport_1 (
    .A(PC), .Din({12{1'b0}}), .str(1'b0), .C(button_1_out), .ld(1'b1), .D(eepromdualport_1_d));
  ALU_visual alu_visual_1 (.A(eepromdualport_1_d[7:0]), .B(S), .S(eepromdualport_1_d[11:8]), .R(alu_visual_1_r));
  registrador_8bits registrador_8bits_1 (
    .D7(alu_visual_1_r[7]), .D6(alu_visual_1_r[6]), .D5(alu_visual_1_r[5]), .D4(alu_visual_1_r[4]),
    .D3(alu_visual_1_r[3]), .D2(alu_visual_1_r[2]), .D1(alu_visual_1_r[1]), .D0(alu_visual_1_r[0]),
    .Clock(button_1_out), .Q7(S[7]), .Q6(S[6]), .Q5(S[5]), .Q4(S[4]), .Q3(S[3]), .Q2(S[2]), .Q1(S[1]),
    .Q0(S[0]));

  // Notes on the sheet:
  //   0 - adiciona 1
  //   1 - soma 3
  //   2 - divide 8 por B
  //   3 - multiplica por 2
  //   0000 = load
  //   0001 = soma
  //   0010 = sub
  //   0011 = multiplicação
  //   0100 = divisão
  //   0101 = shift right
  //   0110 = shift left
  //   0111 = nand
  //   1000 = xor
  //   contents of eepromdualport_1 (hex, n*v repeats v):
  //   1,103,408,302
endmodule
