// Digital circuit NAND-8bits.dig as structural Verilog
module NAND_8bits (
  input  A0,
  input  A1,
  input  A2,
  input  A3,
  input  A4,
  input  A5,
  input  A6,
  input  A7,
  input  B0,
  input  B1,
  input  B2,
  input  B3,
  input  B4,
  input  B5,
  input  B6,
  input  B7,
  output S0,
  output S1,
  output S2,
  output S3,
  output S4,
  output S5,
  output S6,
  output S7
);

  nand nand_1 (S0, A0, B0);
  nand nand_2 (S1, A1, B1);
  nand nand_3 (S2, A2, B2);
  nand nand_4 (S3, A3, B3);
  nand nand_5 (S4, A4, B4);
  nand nand_6 (S5, A5, B5);
  nand nand_7 (S6, A6, B6);
  nand nand_8 (S7, A7, B7);
endmodule
