// Digital circuit PC.dig as structural Verilog
module PC (
  input  Clk,
  input  En,
  output [7:0] Addr
);

  wire add_1_c_o;
  wire [7:0] add_1_s;

  Add #(.Bits(8)) add_1 (.a(Addr), .b(8'h1), .c_i(1'b0), .s(add_1_s), .c_o(add_1_c_o));
  Register #(.Bits(8)) register_1 (.D(add_1_s), .C(Clk), .en(En), .Q(Addr));
  // also tied to GND on the sheet: add_1_c_o
endmodule
