// Digital circuit Seletor.dig as structural Verilog
module Seletor (
  input  [3:0] S,
  output Load,
  output Soma,
  output Sub,
  output Multi,
  output Div,
  output Right,
  output Left,
  output NAND,
  output XOR
);

  wire not_1_out, not_2_out, not_3_out, not_4_out, not_5_out, not_6_out, not_7_out, not_8_out, not_9_out,
       not_10_out, not_11_out, not_12_out, not_13_out, not_14_out, not_15_out, not_16_out, not_17_out,
       not_18_out, not_19_out, not_20_out, not_21_out, not_22_out, not_23_out;

  not not_1 (not_1_out, S[0]);
  not not_2 (not_2_out, S[1]);
  not not_3 (not_3_out, S[2]);
  not not_4 (not_4_out, S[3]);
  not not_5 (not_5_out, S[1]);
  not not_6 (not_6_out, S[2]);
  not not_7 (not_7_out, S[3]);
  not not_8 (not_8_out, S[0]);
  not not_9 (not_9_out, S[2]);
  not not_10 (not_10_out, S[3]);
  and and_1 (Load, not_1_out, not_2_out, not_3_out, not_4_out);
  and and_2 (Soma, S[0], not_5_out, not_6_out, not_7_out);
  and and_3 (Sub, not_8_out, S[1], not_9_out, not_10_out);
  and and_4 (Multi, S[0], S[1], not_11_out, not_12_out);
  not not_11 (not_11_out, S[2]);
  not not_12 (not_12_out, S[3]);
  and and_5 (Div, not_13_out, not_14_out, S[2], not_15_out);
  not not_13 (not_13_out, S[0]);
  not not_14 (not_14_out, S[1]);
  not not_15 (not_15_out, S[3]);
  and and_6 (Right, S[0], not_16_out, S[2], not_17_out);
  not not_16 (not_16_out, S[1]);
  not not_17 (not_17_out, S[3]);
  not not_18 (not_18_out, S[0]);
  not not_19 (not_19_out, S[3]);
  not not_20 (not_20_out, S[3]);
  and and_7 (XOR, not_21_out, not_22_out, not_23_out, S[3]);
  not not_21 (not_21_out, S[0]);
  not not_22 (not_22_out, S[1]);
  not not_23 (not_23_out, S[2]);
  and and_8 (Left, not_18_out, S[1], S[2], not_19_out);
  and and_9 (NAND, S[0], S[1], S[2], not_20_out);

  // Other names for the same wires on the sheet: _0 = S[0]; _1 = S[1]; _2 = S[2]; _3 = S[3]
endmodule
