// Digital circuit contador.dig as structural Verilog
module contador (
  input  clk
);

  wire and_1_out, and_2_out, and_3_out, and_4_out, button_1_out, jk_ff_as_1_nq, q0, q1;
  wire [3:0] driver_1_out, register_1_q, register_2_q, register_3_q, register_4_q;

  and and_1 (and_1_out, ~q0, ~q1);  // And
  and and_2 (and_2_out, ~q0, ~q1);  // And
  and and_3 (and_3_out, ~q0, ~q1);  // And
  and and_4 (and_4_out, ~q0, ~q1);  // And
  Button button_1 (.out(button_1_out));
  JK_FF_AS jk_ff_as_1 (.Set(button_1_out), .J(1'b1), .C(clk), .K(1'b1), .Clr(1'b0), .Q(q0), .nQ(jk_ff_as_1_nq));
  Register #(.Bits(4)) register_1 (.D(4'b0011), .C(clk), .en(1'b1), .Q(register_1_q));
  Register #(.Bits(4)) register_2 (.D(4'b0010), .C(clk), .en(1'b1), .Q(register_2_q));
  Register #(.Bits(4)) register_3 (.D(4'b0011), .C(clk), .en(1'b1), .Q(register_3_q));
  Register #(.Bits(4)) register_4 (.D(4'b0111), .C(clk), .en(1'b1), .Q(register_4_q));
  LED led_1 (.in(q0));
  assign driver_1_out[0] = and_1_out ? register_1_q[0] : 1'bz;  // Driver driver_1
  assign driver_1_out[0] = and_2_out ? register_2_q[0] : 1'bz;  // Driver driver_2
  assign driver_1_out[0] = and_3_out ? register_3_q[0] : 1'bz;  // Driver driver_3
  assign driver_1_out[0] = and_4_out ? register_4_q[0] : 1'bz;  // Driver driver_4
  JK_FF_AS jk_ff_as_2 (.Set(1'b0), .J(1'b1), .C(jk_ff_as_1_nq), .K(1'b1), .Clr(1'b0), .Q(q1));  // open: nQ
  LED led_2 (.in(q1));
  Seven_Seg_Hex seven_seg_hex_1 (.d(driver_1_out), .dp(1'b0));
  // Pins of 1 and 4 bits meet at register_1_q
  // Pins of 1 and 4 bits meet at driver_1_out
  // Pins of 1 and 4 bits meet at register_2_q
  // Pins of 1 and 4 bits meet at register_3_q
  // Pins of 1 and 4 bits meet at register_4_q

  // Other names for the same wires on the sheet: clock = clk
endmodule
