// Digital circuit divisor-8bits.dig as structural Verilog
module divisor_8bits (
  input  A0,
  input  A1,
  input  A2,
  input  A3,
  input  A4,
  input  A5,
  input  A6,
  input  A7,
  input  B0,
  input  B1,
  input  B2,
  input  B3,
  input  B4,
  input  B5,
  input  B6,
  input  B7,
  input  Clock,
  input  Div,
  output S1,
  output S2,
  output S3,
  output S4,
  output S5,
  output S6,
  output S7,
  output S0
);

  wire clear_out, comparator_1_lt, d0, d1, d2, d3, d4, d5, d6, d7, en, jk_ff_1_q, not_1_out, o0, or_1_out,
       q0, q1, q2, q3, q4, q5, q6, q7;
  wire [7:0] multiplexer_1_out, soma_sub_8bits_1_s7;

  Button clear (.out(clear_out));
  registrador_8bits registrador_8bits_1 (
    .D7(d7), .D6(d6), .D5(d5), .D4(d4), .D3(d3), .D2(d2), .D1(d1), .D0(d0), .Clock(Clock), .Q7(q7), .Q6(q6),
    .Q5(q5), .Q4(q4), .Q3(q3), .Q2(q2), .Q1(q1), .Q0(q0));
  Counter #(.Bits(8)) counter_1 (
    .en(o0), .C(Clock), .clr(clear_out), .out({S7, S6, S5, S4, S3, S2, S1, S0}));  // open: ovf
  soma_sub_8bits soma_sub_8bits_1 (
    .A7(q7), .B7(B7), .A6(q6), .B6(B6), .A5(q5), .B5(B5), .A4(q4), .B4(B4), .A3(q3), .B3(B3), .A2(q2),
    .B2(B2), .A1(q1), .B1(B1), .A0(q0), .B0(B0), .SUB(1'b1), .S7(soma_sub_8bits_1_s7[7]),
    .S6(soma_sub_8bits_1_s7[6]), .S5(soma_sub_8bits_1_s7[5]), .S4(soma_sub_8bits_1_s7[4]),
    .S3(soma_sub_8bits_1_s7[3]), .S2(soma_sub_8bits_1_s7[2]), .S1(soma_sub_8bits_1_s7[1]),
    .S0(soma_sub_8bits_1_s7[0]));
  Multiplexer #(.Bits(8)) multiplexer_1 (
    .sel(o0), .in_0({q7, q6, q5, q4, q3, q2, q1, q0}), .in_1(soma_sub_8bits_1_s7), .out(multiplexer_1_out));
  Comparator #(.Bits(8)) comparator_1 (
    .a({q7, q6, q5, q4, q3, q2, q1, q0}), .b({B7, B6, B5, B4, B3, B2, B1, B0}), .lt(comparator_1_lt));  // open: gt, eq
  Multiplexer #(.Bits(8)) multiplexer_2 (
    .sel(Div), .in_0(multiplexer_1_out), .in_1({A7, A6, A5, A4, A3, A2, A1, A0}),
    .out({d7, d6, d5, d4, d3, d2, d1, d0}));
  and and_1 (o0, en, not_1_out);
  not not_1 (not_1_out, comparator_1_lt);
  or or_1 (or_1_out, B0, B1, B2, B3, B4, B5, B6, B7);
  JK_FF jk_ff_1 (.J(Div), .C(Clock), .K(comparator_1_lt), .Q(jk_ff_1_q));  // open: nQ
  and and_2 (en, or_1_out, jk_ff_1_q);
endmodule
