// Digital circuit multiplicador-8bits.dig as structural Verilog
module multiplicador_8bits (
  input  A0,
  input  A1,
  input  A2,
  input  A3,
  input  A4,
  input  A5,
  input  A6,
  input  A7,
  input  B0,
  input  B1,
  input  B2,
  input  B3,
  input  B4,
  input  B5,
  input  B6,
  input  B7,
  output S0,
  output S1,
  output S2,
  output S3,
  output S4,
  output S5,
  output S6,
  output S7,
  output S8,
  output S9,
  output S10,
  output S11,
  output S12,
  output S13,
  output S14,
  output S15
);

  wire and_1_out, and_2_out, and_3_out, and_4_out, and_5_out, and_6_out, and_7_out, and_8_out, and_9_out,
       and_10_out, and_11_out, and_12_out, and_13_out, and_14_out, and_15_out, and_16_out, and_17_out,
       and_18_out, and_19_out, and_20_out, and_21_out, and_22_out, and_23_out, and_24_out, and_26_out,
       and_27_out, and_28_out, and_29_out, and_30_out, and_31_out, and_32_out, and_33_out, and_34_out,
       and_35_out, and_36_out, and_37_out, and_38_out, and_39_out, and_40_out, and_41_out, and_42_out,
       and_43_out, and_44_out, and_45_out, and_46_out, and_47_out, and_48_out, and_49_out, and_50_out,
       and_51_out, and_52_out, and_53_out, and_54_out, and_55_out, and_56_out, and_57_out, and_58_out,
       and_59_out, and_60_out, and_61_out, and_62_out, and_63_out, c1, c2, c3, c4, c5, c6, c7, c8, c9, c10,
       c11, c12, c13, c14, c15, c16, c17, c18, c19, c20, c21, c22, c23, c24, c25, c26, c27, c28, c29, c30,
       c31, c32, c33, c34, c35, c36, c37, c38, c39, c40, c41, c42, c43, c44, c45, c46, c47, c48, c49, c50,
       c51, c52, c53, meia_soma_1_c, meia_soma_1_s, soma_2_s, soma_3_s, soma_4_s, soma_5_s, soma_6_s,
       soma_8_s, soma_9_s, soma_10_s, soma_11_s, soma_13_s, soma_14_s, soma_15_s, soma_16_s, soma_18_s,
       soma_19_s, soma_20_s, soma_21_s, soma_22_s, soma_24_s, soma_25_s, soma_26_s, soma_27_s, soma_28_s,
       soma_29_s, soma_30_s, soma_31_s, soma_32_s, soma_33_s, soma_35_s, soma_36_s, soma_37_s, soma_38_s,
       soma_39_s, soma_41_s, soma_42_s, soma_43_s, soma_44_s, soma_45_s, soma_46_s, soma_47_s, soma_48_s;

  and and_1 (and_1_out, B7, A7);
  soma soma_1 (.A(c47), .B(and_1_out), .Ci(c53), .Co(S15), .S(S14));
  and and_2 (and_2_out, B5, A7);
  soma soma_2 (.A(c31), .B(and_2_out), .Ci(c38), .Co(c39), .S(soma_2_s));
  and and_3 (and_3_out, B6, A7);
  soma soma_3 (.A(c39), .B(and_3_out), .Ci(c46), .Co(c47), .S(soma_3_s));
  and and_4 (and_4_out, B7, A6);
  and and_5 (and_5_out, B3, A7);
  soma soma_4 (.A(c22), .B(and_5_out), .Ci(c14), .Co(c23), .S(soma_4_s));
  and and_6 (and_6_out, B4, A7);
  soma soma_5 (.A(c23), .B(and_6_out), .Ci(c30), .Co(c31), .S(soma_5_s));
  and and_7 (and_7_out, B5, A6);
  and and_8 (and_8_out, B6, A6);
  soma soma_6 (.A(and_8_out), .B(soma_2_s), .Ci(c45), .Co(c46), .S(soma_6_s));
  soma soma_7 (.A(and_4_out), .B(soma_3_s), .Ci(c52), .Co(c53), .S(S13));
  and and_9 (and_9_out, B1, A7);
  meia_soma meia_soma_1 (.A(c7), .B(and_9_out), .S(meia_soma_1_s), .C(meia_soma_1_c));
  and and_10 (and_10_out, B2, A7);
  soma soma_8 (.A(meia_soma_1_c), .B(and_10_out), .Ci(c14), .Co(c15), .S(soma_8_s));
  and and_11 (and_11_out, B3, A6);
  and and_12 (and_12_out, B4, A6);
  soma soma_9 (.A(and_12_out), .B(soma_4_s), .Ci(c29), .Co(c30), .S(soma_9_s));
  soma soma_10 (.A(and_7_out), .B(soma_5_s), .Ci(c37), .Co(c38), .S(soma_10_s));
  and and_13 (and_13_out, B6, A5);
  soma soma_11 (.A(and_13_out), .B(soma_10_s), .Ci(c44), .Co(c45), .S(soma_11_s));
  and and_14 (and_14_out, B7, A5);
  soma soma_12 (.A(and_14_out), .B(soma_6_s), .Ci(c51), .Co(c52), .S(S12));
  and and_15 (and_15_out, B1, A6);
  and and_16 (and_16_out, B2, A6);
  soma soma_13 (.A(and_16_out), .B(meia_soma_1_s), .Ci(c13), .Co(c14), .S(soma_13_s));
  soma soma_14 (.A(and_11_out), .B(soma_8_s), .Ci(c21), .Co(c22), .S(soma_14_s));
  and and_17 (and_17_out, B4, A5);
  soma soma_15 (.A(and_17_out), .B(soma_14_s), .Ci(c28), .Co(c29), .S(soma_15_s));
  and and_18 (and_18_out, B5, A5);
  soma soma_16 (.A(and_18_out), .B(soma_9_s), .Ci(c36), .Co(c37), .S(soma_16_s));
  and and_19 (and_19_out, B6, A4);
  and and_20 (and_20_out, B7, A4);
  soma soma_17 (.A(and_20_out), .B(soma_11_s), .Ci(c50), .Co(c51), .S(S11));
  and and_21 (and_21_out, B0, A7);
  soma soma_18 (.A(and_21_out), .B(and_15_out), .Ci(c6), .Co(c7), .S(soma_18_s));
  and and_22 (and_22_out, B2, A5);
  soma soma_19 (.A(and_22_out), .B(soma_18_s), .Ci(c12), .Co(c13), .S(soma_19_s));
  and and_23 (and_23_out, B3, A5);
  soma soma_20 (.A(and_23_out), .B(soma_13_s), .Ci(c20), .Co(c21), .S(soma_20_s));
  and and_24 (and_24_out, B4, A4);
  and and_25 (soma_15_s, B5, A4);
  soma soma_21 (.A(soma_15_s), .B(soma_15_s), .Ci(c35), .Co(c36), .S(soma_21_s));
  soma soma_22 (.A(and_19_out), .B(soma_16_s), .Ci(c43), .Co(c44), .S(soma_22_s));
  and and_26 (and_26_out, B7, A3);
  soma soma_23 (.A(and_26_out), .B(soma_22_s), .Ci(c49), .Co(c50), .S(S10));
  and and_27 (and_27_out, B0, A6);
  and and_28 (and_28_out, B1, A5);
  soma soma_24 (.A(and_27_out), .B(and_28_out), .Ci(c5), .Co(c6), .S(soma_24_s));
  and and_29 (and_29_out, B2, A4);
  and and_30 (and_30_out, B3, A4);
  soma soma_25 (.A(and_30_out), .B(soma_19_s), .Ci(c19), .Co(c20), .S(soma_25_s));
  soma soma_26 (.A(and_24_out), .B(soma_20_s), .Ci(c27), .Co(c28), .S(soma_26_s));
  and and_31 (and_31_out, B5, A3);
  soma soma_27 (.A(and_31_out), .B(soma_26_s), .Ci(c34), .Co(c35), .S(soma_27_s));
  and and_32 (and_32_out, B6, A3);
  soma soma_28 (.A(and_32_out), .B(soma_21_s), .Ci(c42), .Co(c43), .S(soma_28_s));
  and and_33 (and_33_out, B7, A2);
  and and_34 (and_34_out, B0, A5);
  and and_35 (and_35_out, B1, A4);
  soma soma_29 (.A(and_34_out), .B(and_35_out), .Ci(c4), .Co(c5), .S(soma_29_s));
  soma soma_30 (.A(and_29_out), .B(soma_24_s), .Ci(c11), .Co(c12), .S(soma_30_s));
  and and_36 (and_36_out, B3, A3);
  soma soma_31 (.A(and_36_out), .B(soma_30_s), .Ci(c18), .Co(c19), .S(soma_31_s));
  and and_37 (and_37_out, B4, A3);
  soma soma_32 (.A(and_37_out), .B(soma_25_s), .Ci(c26), .Co(c27), .S(soma_32_s));
  and and_38 (and_38_out, B5, A2);
  and and_39 (and_39_out, B6, A2);
  soma soma_33 (.A(and_39_out), .B(soma_27_s), .Ci(c41), .Co(c42), .S(soma_33_s));
  soma soma_34 (.A(and_33_out), .B(soma_28_s), .Ci(c48), .Co(c49), .S(S9));
  and and_40 (and_40_out, B1, A3);
  soma soma_35 (.A(and_46_out), .B(and_40_out), .Ci(c3), .Co(c4), .S(soma_35_s));
  and and_41 (and_41_out, B2, A3);
  soma soma_36 (.A(and_41_out), .B(soma_29_s), .Ci(c10), .Co(c11), .S(soma_36_s));
  and and_42 (and_42_out, B3, A2);
  and and_43 (and_43_out, B4, A2);
  soma soma_37 (.A(and_43_out), .B(soma_31_s), .Ci(c25), .Co(c26), .S(soma_37_s));
  soma soma_38 (.A(and_38_out), .B(soma_32_s), .Ci(c33), .Co(c34), .S(soma_38_s));
  and and_44 (and_44_out, B6, A1);
  soma soma_39 (.A(and_44_out), .B(soma_38_s), .Ci(c40), .Co(c41), .S(soma_39_s));
  and and_45 (and_45_out, B7, A1);
  soma soma_40 (.A(and_45_out), .B(soma_33_s), .Ci(c47), .Co(c48), .S(S8));
  and and_46 (and_46_out, B0, A4);
  and and_47 (and_47_out, B1, A2);
  and and_48 (and_48_out, B2, A2);
  soma soma_41 (.A(and_48_out), .B(soma_35_s), .Ci(c9), .Co(c10), .S(soma_41_s));
  soma soma_42 (.A(and_42_out), .B(soma_36_s), .Ci(c17), .Co(c18), .S(soma_42_s));
  and and_49 (and_49_out, B4, A1);
  soma soma_43 (.A(and_49_out), .B(soma_42_s), .Ci(c24), .Co(c25), .S(soma_43_s));
  and and_50 (and_50_out, B5, A1);
  soma soma_44 (.A(and_50_out), .B(soma_37_s), .Ci(c32), .Co(c33), .S(soma_44_s));
  and and_51 (and_51_out, B6, A0);
  and and_52 (and_52_out, B7, A0);
  meia_soma meia_soma_2 (.A(and_52_out), .B(soma_39_s), .S(S7), .C(c47));
  and and_53 (and_53_out, B0, A3);
  soma soma_45 (.A(and_53_out), .B(and_47_out), .Ci(c2), .Co(c3), .S(soma_45_s));
  and and_54 (and_54_out, B2, A1);
  soma soma_46 (.A(and_54_out), .B(soma_45_s), .Ci(c8), .Co(c9), .S(soma_46_s));
  and and_55 (and_55_out, B3, A1);
  soma soma_47 (.A(and_55_out), .B(soma_41_s), .Ci(c16), .Co(c17), .S(soma_47_s));
  and and_56 (and_56_out, B4, A0);
  and and_57 (and_57_out, B5, A0);
  meia_soma meia_soma_3 (.A(and_57_out), .B(soma_43_s), .S(S5), .C(c32));
  meia_soma meia_soma_4 (.A(and_51_out), .B(soma_44_s), .S(S6), .C(c40));
  and and_58 (and_58_out, B0, A2);
  and and_59 (and_59_out, B1, A1);
  soma soma_48 (.A(and_58_out), .B(and_59_out), .Ci(c1), .Co(c2), .S(soma_48_s));
  and and_60 (and_60_out, B2, A0);
  and and_61 (and_61_out, B3, A0);
  meia_soma meia_soma_5 (.A(and_61_out), .B(soma_46_s), .S(S3), .C(c16));
  meia_soma meia_soma_6 (.A(and_56_out), .B(soma_47_s), .S(S4), .C(c24));
  and and_62 (and_62_out, B0, A1);
  and and_63 (and_63_out, B1, A0);
  meia_soma meia_soma_7 (.A(and_62_out), .B(and_63_out), .S(S1), .C(c1));
  meia_soma meia_soma_8 (.A(and_60_out), .B(soma_48_s), .S(S2), .C(c8));
  and and_64 (S0, B0, A0);
endmodule
