// Digital circuit shitfer-completo-8bits.dig as structural Verilog
module shitfer_completo_8bits (
  input  A3,
  input  A0,
  input  A1,
  input  A2,
  input  right,
  input  left,
  input  A4,
  input  A5,
  input  A6,
  input  A7,
  input  shift,
  output S0,
  output S1,
  output S2,
  output S3,
  output S4,
  output S5,
  output S6,
  output S7
);

  wire multiplexer_1_out, multiplexer_2_out, multiplexer_3_out, multiplexer_4_out, multiplexer_5_out,
       multiplexer_6_out, multiplexer_7_out, multiplexer_8_out;
  wire [1:0] not_1_out;

  not not_1 (not_1_out[0], left);
  not not_2 (not_1_out[1], right);
  Multiplexer #(.Selector_Bits(2)) multiplexer_1 (
    .sel(not_1_out), .in_0(S7), .in_1(1'b0), .in_2(S6), .in_3(A7), .out(multiplexer_1_out));
  Multiplexer #(.Selector_Bits(2)) multiplexer_2 (
    .sel(not_1_out), .in_0(S6), .in_1(S7), .in_2(S5), .in_3(A6), .out(multiplexer_2_out));
  Multiplexer #(.Selector_Bits(2)) multiplexer_3 (
    .sel(not_1_out), .in_0(S5), .in_1(S6), .in_2(S4), .in_3(A5), .out(multiplexer_3_out));
  Multiplexer #(.Selector_Bits(2)) multiplexer_4 (
    .sel(not_1_out), .in_0(S4), .in_1(S5), .in_2(S3), .in_3(A4), .out(multiplexer_4_out));
  Multiplexer #(.Selector_Bits(2)) multiplexer_5 (
    .sel(not_1_out), .in_0(S3), .in_1(S4), .in_2(S2), .in_3(A3), .out(multiplexer_5_out));
  Multiplexer #(.Selector_Bits(2)) multiplexer_6 (
    .sel(not_1_out), .in_0(S2), .in_1(S3), .in_2(S1), .in_3(A2), .out(multiplexer_6_out));
  Multiplexer #(.Selector_Bits(2)) multiplexer_7 (
    .sel(not_1_out), .in_0(S1), .in_1(S2), .in_2(S0), .in_3(A1), .out(multiplexer_7_out));
  Multiplexer #(.Selector_Bits(2)) multiplexer_8 (
    .sel(not_1_out), .in_0(S0), .in_1(S1), .in_2(1'b0), .in_3(A0), .out(multiplexer_8_out));
  D_FF d_ff_1 (.D(multiplexer_1_out), .C(shift), .Q(S7));  // open: nQ
  D_FF d_ff_2 (.D(multiplexer_2_out), .C(shift), .Q(S6));  // open: nQ
  D_FF d_ff_3 (.D(multiplexer_3_out), .C(shift), .Q(S5));  // open: nQ
  D_FF d_ff_4 (.D(multiplexer_4_out), .C(shift), .Q(S4));  // open: nQ
  D_FF d_ff_5 (.D(multiplexer_5_out), .C(shift), .Q(S3));  // open: nQ
  D_FF d_ff_6 (.D(multiplexer_6_out), .C(shift), .Q(S2));  // open: nQ
  D_FF d_ff_7 (.D(multiplexer_7_out), .C(shift), .Q(S1));  // open: nQ
  D_FF d_ff_8 (.D(multiplexer_8_out), .C(shift), .Q(S0));  // open: nQ
endmodule
