// Digital circuit soma-8bits.dig as structural Verilog
module soma_8bits (
  input  A7,
  input  B7,
  input  A6,
  input  B6,
  input  A5,
  input  B5,
  input  A4,
  input  B4,
  input  A3,
  input  B3,
  input  A2,
  input  B2,
  input  A1,
  input  B1,
  input  A0,
  input  B0,
  output S0,
  output S1,
  output S2,
  output S3,
  output S4,
  output S5,
  output S6,
  output S7,
  output Co
);

  wire soma_2_co, soma_3_co, soma_4_co, soma_5_co, soma_6_co, soma_7_co, soma_8_co;

  soma soma_1 (.A(A7), .B(B7), .Ci(soma_2_co), .Co(Co), .S(S7));
  soma soma_2 (.A(A6), .B(B6), .Ci(soma_3_co), .Co(soma_2_co), .S(S6));
  soma soma_3 (.A(A5), .B(B5), .Ci(soma_4_co), .Co(soma_3_co), .S(S5));
  soma soma_4 (.A(A4), .B(B4), .Ci(soma_5_co), .Co(soma_4_co), .S(S4));
  soma soma_5 (.A(A3), .B(B3), .Ci(soma_6_co), .Co(soma_5_co), .S(S3));
  soma soma_6 (.A(A2), .B(B2), .Ci(soma_7_co), .Co(soma_6_co), .S(S2));
  soma soma_7 (.A(A1), .B(B1), .Ci(soma_8_co), .Co(soma_7_co), .S(S1));
  soma soma_8 (.A(A0), .B(B0), .Ci(1'b0), .Co(soma_8_co), .S(S0));
endmodule
