// Digital circuit soma.dig as structural Verilog
module soma (
  input  A,
  input  B,
  input  Ci,
  output Co,
  output S
);

  wire meia_soma_1_c, meia_soma_1_s, meia_soma_2_c;

  meia_soma meia_soma_1 (.A(A), .B(B), .S(meia_soma_1_s), .C(meia_soma_1_c));
  meia_soma meia_soma_2 (.A(Ci), .B(meia_soma_1_s), .S(S), .C(meia_soma_2_c));
  or or_1 (Co, meia_soma_1_c, meia_soma_2_c);
endmodule
