// Digital circuit soma_sub-8bits.dig as structural Verilog
module soma_sub_8bits (
  input  SUB,
  input  B0,
  input  B1,
  input  B2,
  input  B3,
  input  B4,
  input  B5,
  input  B6,
  input  B7,
  input  A0,
  input  A1,
  input  A2,
  input  A3,
  input  A4,
  input  A5,
  input  A6,
  input  A7,
  output S0,
  output S1,
  output S2,
  output S3,
  output S4,
  output S5,
  output S6,
  output S7
);

  wire soma_2_co, soma_3_co, soma_4_co, soma_5_co, soma_6_co, soma_7_co, soma_8_co, xor_1_out, xor_2_out,
       xor_3_out, xor_4_out, xor_5_out, xor_6_out, xor_7_out, xor_8_out;

  xor xor_1 (xor_1_out, B7, SUB);
  xor xor_2 (xor_2_out, B6, SUB);
  xor xor_3 (xor_3_out, B5, SUB);
  xor xor_4 (xor_4_out, B4, SUB);
  xor xor_5 (xor_5_out, B3, SUB);
  xor xor_6 (xor_6_out, B2, SUB);
  xor xor_7 (xor_7_out, B1, SUB);
  xor xor_8 (xor_8_out, B0, SUB);
  soma soma_1 (.A(A7), .B(xor_1_out), .Ci(soma_2_co), .S(S7));  // open: Co
  soma soma_2 (.A(A6), .B(xor_2_out), .Ci(soma_3_co), .Co(soma_2_co), .S(S6));
  soma soma_3 (.A(A5), .B(xor_3_out), .Ci(soma_4_co), .Co(soma_3_co), .S(S5));
  soma soma_4 (.A(A4), .B(xor_4_out), .Ci(soma_5_co), .Co(soma_4_co), .S(S4));
  soma soma_5 (.A(A3), .B(xor_5_out), .Ci(soma_6_co), .Co(soma_5_co), .S(S3));
  soma soma_6 (.A(A2), .B(xor_6_out), .Ci(soma_7_co), .Co(soma_6_co), .S(S2));
  soma soma_7 (.A(A1), .B(xor_7_out), .Ci(soma_8_co), .Co(soma_7_co), .S(S1));
  soma soma_8 (.A(A0), .B(xor_8_out), .Ci(SUB), .Co(soma_8_co), .S(S0));
endmodule
